// Logisim project alu_test_2.circ as structural Verilog: 1 circuit, main circuit main
module main (
  input  [7:0] in_1
);

  wire and_1_out, and_2_out, and_3_out, and_4_out, and_5_out, and_6_out, and_7_out, and_8_out, and_9_out,
       and_10_out, and_11_out, and_12_out, and_13_out, and_14_out, and_15_out, and_16_out;
  wire [4:0] not_2_out;
  wire [5:0] not_4_out, not_7_out, not_8_out;
  wire [6:0] not_1_out, not_3_out, not_5_out, not_6_out;

  and and_1 (and_1_out, and_2_out, in_1[0], in_1[1], in_1[2]);
  and and_2 (and_2_out, not_2_out[4], not_2_out[3], not_2_out[2], not_2_out[1], not_2_out[0]);
  assign not_1_out = ~{in_1[1], in_1[7:4], in_1[1:0]};  // NOT_Gate not_1, 7 bits wide
  and and_3 (and_3_out, not_4_out[5], not_4_out[4], not_4_out[3], not_4_out[2], not_4_out[1], not_4_out[0]);
  assign not_2_out = ~in_1[7:3];  // NOT_Gate not_2, 5 bits wide
  assign not_3_out = ~{in_1[7:2], in_1[0]};  // NOT_Gate not_3, 7 bits wide
  and and_4 (and_4_out, not_3_out[6], not_3_out[5], not_3_out[4], not_3_out[3], not_3_out[2], not_3_out[1], not_3_out[0]);
  and and_5 (and_5_out, not_1_out[0], not_1_out[1], not_1_out[2], not_1_out[3], not_1_out[4], not_1_out[5], not_1_out[6]);
  assign not_4_out = ~{in_1[2], in_1[3], in_1[4], in_1[5], in_1[6], in_1[7]};  // NOT_Gate not_4, 6 bits wide
  and and_6 (and_6_out, and_5_out, in_1[3]);
  and and_7 (and_7_out, and_3_out, in_1[1], in_1[0]);
  assign not_5_out = ~in_1[7:1];  // NOT_Gate not_5, 7 bits wide
  assign not_6_out = ~{in_1[1:0], in_1[3], in_1[4], in_1[5], in_1[6], in_1[7]};  // NOT_Gate not_6, 7 bits wide
  and and_8 (and_8_out, in_1[1], and_4_out);
  assign not_7_out = ~{in_1[1], in_1[3], in_1[4], in_1[5], in_1[6], in_1[7]};  // NOT_Gate not_7, 6 bits wide
  assign not_8_out = ~{in_1[0], in_1[7:3]};  // NOT_Gate not_8, 6 bits wide
  and and_9 (and_9_out, not_5_out[0], not_5_out[1], not_5_out[2], not_5_out[3], not_5_out[4], not_5_out[5], not_5_out[6]);
  and and_10 (and_10_out, not_6_out[0], not_6_out[1], not_6_out[2], not_6_out[3], not_6_out[4], not_6_out[5], not_6_out[6]);
  and and_11 (and_11_out, in_1[0], and_9_out);
  and and_12 (and_12_out, in_1[2], and_10_out);
  and and_13 (and_13_out, in_1[2], in_1[0], and_14_out);
  and and_14 (and_14_out, not_7_out[0], not_7_out[1], not_7_out[2], not_7_out[3], not_7_out[4], not_7_out[5]);
  and and_15 (and_15_out, in_1[2], in_1[1], and_16_out);
  and and_16 (and_16_out, not_8_out[0], not_8_out[1], not_8_out[2], not_8_out[3], not_8_out[4], not_8_out[5]);
  LedBar ledbar_1 (
    .led0(and_11_out), .led1(and_8_out), .led2(and_7_out), .led3(and_12_out), .led4(and_13_out),
    .led5(and_15_out), .led6(and_1_out), .led7(and_6_out));
endmodule
