// Logisim project cpu_base_test1.circ as structural Verilog: 1 circuit, main circuit main
module main (
  input  [7:0] X,
  input  [7:0] Y,
  input  in_3,
  output [7:0] out_4,
  output [7:0] out_5,
  output [7:0] out_6
);

  wire clock_1_out, transistor_1_out;
  wire [7:0] NOT_Y_TUNNEL;

  Clock clock_1 (.out(clock_1_out));
  Adder adder_1 (.a(X), .b(Y), .out(out_5));  // open: cin, cout
  Transistor transistor_1 (.in(1'b1), .out(transistor_1_out), .gate(in_3));
  Shifter shifter_1 (.in(X), .\dist (3'b001), .out(out_6));
  assign NOT_Y_TUNNEL = ~Y;  // NOT_Gate NOT_Y, 8 bits wide
  Adder adder_2 (.a(X), .b(NOT_Y_TUNNEL), .out(out_4), .cin(1'b1));  // open: cout
  Transistor transistor_2 (.in(1'b1), .out(transistor_1_out), .gate(clock_1_out));
  Pull_Resistor pull_resistor_1 (.node(transistor_1_out));
  LED led_1 (.in(transistor_1_out));
endmodule
