// Logisim project cpu_test_1.circ as structural Verilog: 5 circuits, main circuit main
module main (
  input  in_1,
  input  in_2,
  input  in_3,
  input  in_4,
  input  in_5,
  input  in_6,
  input  in_7,
  input  [3:0] in_8,
  input  [3:0] in_9,
  input  [3:0] in_10,
  input  [3:0] in_11,
  input  [13:0] AF,
  input  [6:0] AS,
  input  [3:0] A,
  input  [3:0] B,
  input  [3:0] C,
  input  [7:0] BS,
  input  [13:0] BF,
  input  [6:0] CS,
  output [3:0] out_20,
  output [3:0] out_21,
  output [3:0] out_22,
  output [3:0] out_23
);

  wire and_1_out, and_2_out, and_3_out, and_4_out, and_5_out, and_6_out, and_11_out, and_12_out, and_13_out,
       and_14_out, and_15_out, and_16_out, and_17_out, and_18_out, and_19_out, and_20_out, and_21_out,
       and_22_out, and_23_out, and_24_out, and_25_out, and_26_out, and_27_out, and_28_out, and_29_out,
       and_30_out, and_31_out, and_32_out, and_33_out, and_34_out, and_35_out, and_36_out, and_37_out,
       and_38_out, and_39_out, and_40_out, and_41_out, and_42_out, and_43_out, and_44_out, and_45_out,
       and_46_out, and_47_out, and_52_out, and_53_out, and_58_out, and_59_out, and_60_out, and_61_out,
       not_1_out, not_2_out, not_3_out, not_4_out, not_5_out, not_6_out, not_7_out, not_8_out, not_9_out,
       not_10_out, not_11_out, not_12_out, not_13_out, not_14_out, not_15_out, not_16_out, not_17_out,
       not_18_out, not_19_out, not_20_out, not_21_out, not_22_out, or_1_out;
  wire [3:0] and_48_out, and_56_out, TUNNEL_OPCODE;
  wire [3:3] clock_1_out;

  not not_1 (not_1_out, in_7);
  Clock clock_1 (.out(clock_1_out[3]));
  and and_1 (and_1_out, in_5, in_6);
  not not_2 (not_2_out, in_7);
  not not_3 (not_3_out, and_1_out);
  and and_2 (and_2_out, not_3_out, in_5);
  and and_3 (and_3_out, and_1_out, not_1_out);
  LED oof (.in(and_3_out));
  and and_4 (and_4_out, in_6, not_3_out);
  not not_4 (not_4_out, and_3_out);
  and and_5 (and_5_out, not_2_out, and_4_out);
  LED fof (.in(and_5_out));
  and and_6 (and_6_out, and_1_out, not_4_out);
  LED ooo (.in(and_6_out));
  assign TUNNEL_OPCODE = {4{clock_1_out[3]}} & in_8;  // AND_Gate and_7, 4 bits wide
  assign out_21 = {4{clock_1_out[3]}} & in_9;  // AND_Gate and_8, 4 bits wide
  assign out_22 = {4{clock_1_out[3]}} & in_10;  // AND_Gate and_9, 4 bits wide
  assign out_23 = {4{clock_1_out[3]}} & in_11;  // AND_Gate and_10, 4 bits wide
  not not_5 (not_5_out, and_4_out);
  and and_11 (and_11_out, in_7, and_4_out);
  and and_12 (and_12_out, and_2_out, not_1_out);
  and and_13 (and_13_out, and_2_out, in_7);
  not not_6 (not_6_out, in_5);
  and and_14 (and_14_out, in_7, not_5_out);
  LED foo (.in(and_11_out));
  LED off (.in(and_12_out));
  LED ofo (.in(and_13_out));
  and and_15 (and_15_out, not_6_out, and_14_out);
  LED ffo (.in(and_15_out));
  not not_7 (not_7_out, in_1);
  not not_8 (not_8_out, in_4);
  not not_9 (not_9_out, TUNNEL_OPCODE[0]);
  not not_10 (not_10_out, TUNNEL_OPCODE[3]);
  buf and_16 (and_16_out, not_7_out);  // AND_Gate
  and and_17 (and_17_out, in_1, in_2);
  and and_18 (and_18_out, in_3, not_8_out);
  LED fo (.in(and_18_out));
  not not_11 (not_11_out, TUNNEL_OPCODE[1]);
  not not_12 (not_12_out, TUNNEL_OPCODE[0]);
  and and_19 (and_19_out, TUNNEL_OPCODE[1], not_9_out);
  not not_13 (not_13_out, TUNNEL_OPCODE[2]);
  not not_14 (not_14_out, TUNNEL_OPCODE[1]);
  not not_15 (not_15_out, TUNNEL_OPCODE[3]);
  and and_20 (and_20_out, TUNNEL_OPCODE[3], TUNNEL_OPCODE[2]);
  not not_16 (not_16_out, TUNNEL_OPCODE[2]);
  and and_21 (and_21_out, TUNNEL_OPCODE[2], TUNNEL_OPCODE[1]);
  not not_17 (not_17_out, TUNNEL_OPCODE[3]);
  or or_1 (or_1_out, and_16_out, and_17_out);
  and and_22 (and_22_out, TUNNEL_OPCODE[1], TUNNEL_OPCODE[0]);
  and and_23 (and_23_out, not_11_out, not_12_out);
  and and_24 (and_24_out, not_14_out, TUNNEL_OPCODE[0]);
  and and_25 (and_25_out, not_15_out, TUNNEL_OPCODE[2]);
  and and_26 (and_26_out, TUNNEL_OPCODE[3], not_16_out);
  and and_27 (and_27_out, not_17_out, not_10_out);
  LED led_1 (.in(or_1_out));
  and and_28 (and_28_out, not_15_out, not_13_out);
  not not_18 (not_18_out, and_22_out);
  and and_29 (and_29_out, and_24_out, and_25_out);
  and and_30 (and_30_out, and_21_out, and_27_out);
  and and_31 (and_31_out, not_17_out, and_21_out);
  and and_32 (and_32_out, and_19_out, and_28_out);
  and and_33 (and_33_out, and_28_out, and_24_out);
  and and_34 (and_34_out, not_18_out, and_26_out);
  and and_35 (and_35_out, and_23_out, and_20_out);
  not not_19 (not_19_out, and_23_out);
  not not_20 (not_20_out, TUNNEL_OPCODE[0]);
  and and_36 (and_36_out, TUNNEL_OPCODE[0], and_31_out);
  and and_37 (and_37_out, and_23_out, and_25_out);
  and and_38 (and_38_out, and_28_out, and_22_out);
  and and_39 (and_39_out, and_34_out, not_19_out);
  and and_40 (and_40_out, and_26_out, and_23_out);
  and and_41 (and_41_out, not_20_out, and_30_out);
  not not_21 (not_21_out, and_25_out);
  and and_42 (and_42_out, and_23_out, not_21_out);
  LED ffff (.in(and_43_out));
  LED offf (.in(and_33_out));
  LED foff (.in(and_32_out));
  LED ooff (.in(and_38_out));
  LED ffof (.in(and_37_out));
  LED ofof (.in(and_29_out));
  LED foof (.in(and_41_out));
  LED ooof (.in(and_36_out));
  LED fffo (.in(and_40_out));
  LED fofo (.in(and_39_out));
  LED ffoo (.in(and_35_out));
  LED oooo (.in(and_45_out));
  not not_22 (not_22_out, TUNNEL_OPCODE[3]);
  and and_43 (and_43_out, and_42_out, not_22_out);
  and and_44 (and_44_out, and_22_out, and_21_out);
  and and_45 (and_45_out, and_44_out, TUNNEL_OPCODE[3]);
  // Buzzer #(.smooth_width(1)) buzzer_1: pin names not known; wires that end beside it: BS, BF, and_35_out, CS
  and and_46 (and_46_out, out_22[1], and_33_out);
  and and_47 (and_47_out, out_22[0], and_33_out);
  and and_48 (and_48_out[0], and_32_out, out_23[0]);
  and and_49 (and_48_out[1], out_23[1], and_32_out);
  and and_50 (and_56_out[2], out_22[2], and_32_out);
  and and_51 (and_56_out[3], out_22[3], and_32_out);
  and and_52 (and_52_out, out_23[1], and_33_out);
  and and_53 (and_53_out, out_23[3], and_33_out);
  and and_54 (and_48_out[2], out_23[2], and_32_out);
  and and_55 (and_48_out[3], out_23[3], and_32_out);
  and and_56 (and_56_out[0], and_32_out, out_22[0]);
  and and_57 (and_56_out[1], out_22[1], and_32_out);
  Hex_Digit_Display hex_digit_display_1 (.value(and_48_out));  // open: dp
  Hex_Digit_Display hex_digit_display_2 (.value(and_56_out));  // open: dp
  and and_58 (and_58_out, out_23[2], and_33_out);
  and and_59 (and_59_out, out_22[3], and_33_out);
  and and_60 (and_60_out, and_33_out, out_22[2]);
  and and_61 (and_61_out, out_23[0], and_33_out);
  or or_2 (out_20[0], and_61_out, and_47_out);
  or or_3 (out_20[1], and_52_out, and_46_out);
  or or_4 (out_20[2], and_58_out, and_60_out);
  or or_5 (out_20[3], and_53_out, and_59_out);

  // Other names for the same wires on the sheet: ADD_RESULT[3:0] = out_20; TUNNEL_A[3:0] = out_23;
  //   TUNNEL_A_d[3:0] = A; TUNNEL_AF[13:0] = AF; TUNNEL_AS[6:0] = AS; TUNNEL_B[3:0] = out_22; TUNNEL_B_d[3:0] = B;
  //   TUNNEL_BF[13:0] = BF; TUNNEL_BS[7:0] = BS; TUNNEL_C[3:0] = out_21; TUNNEL_C_d[3:0] = C; TUNNEL_CS[6:0] = CS

  // Notes on the sheet:
  //   ALU v1
  //   TESTING CIRCUIT
  //   inputs
  //   14 bits
  //   ALU
  //   Audio
  //   7&8 bits
  //   4 bits
  //   Sound
  //   Binary decoder
  //   4-bit adder. TUNNEL_A + TUNNEL_B
  //   <- DECODED A
  //   <- DECODED B
  //   <-- ALU result
endmodule

module adder_c (
  input  in_1,
  input  A_1,
  input  B_1,
  input  [3:0] A,
  input  [3:0] B,
  output Result_1,
  output Carry_1,
  output [3:0] Result
);

  wire and_1_out, and_2_out, xor_1_out;

  and and_1 (and_1_out, A_1, B_1);
  xor xor_1 (xor_1_out, A_1, B_1);
  or or_1 (Carry_1, and_1_out, and_2_out);
  and and_2 (and_2_out, in_1, xor_1_out);
  or or_2 (Result[0], A[0], B[0]);
  or or_3 (Result[1], A[1], B[1]);
  or or_4 (Result[2], A[2], B[2]);
  or or_5 (Result[3], A[3], B[3]);
  xor xor_2 (Result_1, in_1, xor_1_out);
endmodule

module decoder_c (
  input  in_1,
  input  in_2,
  input  [3:0] in_3,
  output out_4
);

  wire and_1_out, and_2_out, and_3_out, not_1_out, not_2_out;

  not not_1 (not_1_out, in_1);
  not not_2 (not_2_out, in_2);
  and and_1 (and_1_out, not_1_out, not_2_out);
  and and_2 (and_2_out, not_1_out, in_2);
  and and_3 (and_3_out, in_1, not_2_out);
  and and_4 (out_4, in_1, in_2);
  _7_Segment_Display u_7_segment_display_1 (
    .f(and_1_out), .a(and_1_out), .b(and_1_out), .e(and_1_out), .d(and_1_out), .c(and_1_out));  // open: g, dp
  Hex_Digit_Display hex_digit_display_1 (.value(in_3));  // open: dp
endmodule

module extender_c (
  input  in_1,
  output [3:0] out_2
);


  assign out_2 = {4{in_1}};
endmodule

module rom_c_test (
  input  [3:0] in_1,
  input  [3:0] in_2,
  output [3:0] out_3,
  output [3:0] out_4,
  output [3:0] out_5,
  output [3:0] out_6
);

  wire and_1_out, and_2_out, and_4_out, and_5_out, and_6_out, and_7_out, and_8_out, and_9_out, and_10_out,
       and_11_out, and_12_out, and_13_out, and_14_out, and_15_out, and_16_out, and_17_out, and_18_out,
       and_19_out, and_20_out, and_21_out, and_22_out, and_23_out, and_24_out, and_25_out, clock_1_out,
       not_1_out, not_2_out, not_3_out;
  wire [3:0] TUNNEL_A, TUNNEL_B, TUNNEL_C;

  Clock #(.highDuration(1000)) clock_1 (.out(clock_1_out));
  and and_1 (and_1_out, out_4[1], clock_1_out);
  not not_1 (not_1_out, out_4[0]);
  and and_2 (and_2_out, out_5[0], clock_1_out);
  buf and_3 (out_5[0], not_1_out);  // AND_Gate
  and and_4 (and_4_out, out_4[1], clock_1_out);
  and and_5 (and_5_out, out_4[3], clock_1_out);
  and and_6 (and_6_out, out_4[2], clock_1_out);
  and and_7 (and_7_out, out_4[3], clock_1_out);
  and and_8 (and_8_out, clock_1_out, out_4[2]);
  and and_9 (and_9_out, out_4[0], clock_1_out);
  or or_1 (out_4[0], and_9_out, and_2_out);
  or or_2 (out_4[1], and_4_out, and_1_out);
  or or_3 (out_4[2], and_6_out, and_8_out);
  or or_4 (out_4[3], and_5_out, and_7_out);
  ROM #(.addrWidth(4), .dataWidth(4)) rom_1 (.addr(out_4), .data(TUNNEL_A));
  not not_2 (not_2_out, out_4[0]);
  and and_10 (and_10_out, out_4[1], clock_1_out);
  and and_11 (and_11_out, not_2_out, clock_1_out);
  and and_12 (and_12_out, in_1[1], clock_1_out);
  and and_13 (and_13_out, in_1[3], clock_1_out);
  and and_14 (and_14_out, in_1[2], clock_1_out);
  and and_15 (and_15_out, out_4[3], clock_1_out);
  and and_16 (and_16_out, clock_1_out, out_4[2]);
  and and_17 (and_17_out, in_1[0], clock_1_out);
  not not_3 (not_3_out, out_3[0]);
  ROM #(.addrWidth(4), .dataWidth(4)) rom_2 (.addr(out_3), .data(TUNNEL_B));
  or or_5 (out_3[0], and_17_out, and_11_out);
  or or_6 (out_3[1], and_12_out, and_10_out);
  or or_7 (out_3[2], and_14_out, and_16_out);
  or or_8 (out_3[3], and_13_out, and_15_out);
  and and_18 (and_18_out, out_3[1], clock_1_out);
  and and_19 (and_19_out, not_3_out, clock_1_out);
  and and_20 (and_20_out, in_2[1], clock_1_out);
  and and_21 (and_21_out, in_2[3], clock_1_out);
  and and_22 (and_22_out, in_2[2], clock_1_out);
  and and_23 (and_23_out, out_3[3], clock_1_out);
  and and_24 (and_24_out, clock_1_out, out_3[2]);
  and and_25 (and_25_out, in_2[0], clock_1_out);
  ROM #(.addrWidth(4), .dataWidth(4)) rom_3 (.addr(out_6), .data(TUNNEL_C));
  or or_9 (out_6[0], and_25_out, and_19_out);
  or or_10 (out_6[1], and_20_out, and_18_out);
  or or_11 (out_6[2], and_22_out, and_24_out);
  or or_12 (out_6[3], and_21_out, and_23_out);

  assign out_5[3:1] = out_4[3:1];

  // Other names for the same wires on the sheet: ROM_ID[3:0] = out_4; ROM_ID_s[3:0] = {out_4[3:1], out_5[0]}

  // Notes on the sheet:
  //   contents of rom_1 (hex, n*v repeats v):
  //   9 2 2 1 3 2 1 3 4*0 1 2
  //   OP A B BF CS BS
  //   0010
  //   contents of rom_2 (hex, n*v repeats v):
  //   9 2 2 1 3 2 1 3 4*0 1 2
  //   OP A B BF CS BS
  //   0011
  //   contents of rom_3 (hex, n*v repeats v):
  //   9 2 2 1 3 2 1 3 4*0 1 2
  //   OP A B BF CS BS
endmodule
